# Fritzing sketch KY-009 (saved by Fritzing 0.9.3b)
breadboards: 1

parts:
  Part1 = KY-009 Full Color RGB LED SMD Module [package="Breakout board"]
  Componente1 = Arduino Nano (Rev3.0)
  R2 = Resistor [tolerance=±5% resistance=220 package="0402 [SMD]"]
  R3 = Resistor [tolerance=±5% resistance=220 package="0402 [SMD]"]
  R4 = Resistor [tolerance=±5% resistance=220 package="0402 [SMD]"]

nets:
  N1: Part1.-, Componente1.5V
  N2: Part1.R, R4.Pin_1
  N3: Part1.G, R3.Pin_1
  N4: Part1.B, R2.Pin_1
  N5: Componente1.D9, R2.Pin_0
  N6: Componente1.D10, R3.Pin_0
  N7: Componente1.D11/MOSI, R4.Pin_0

custom parts:
  KY-009 Full Color RGB LED SMD Module: RGB full color LED Module KY-009 for Arduino, emits a range of colors by mixing red, green and blue. The amount of each primary color is adjusted using PWM.
