# Fritzing sketch KY-011 (saved by Fritzing 0.9.3b)
breadboards: 1

parts:
  Part1 = KY-011 Two Color LED Module [package="Breakout board"]
  Componente1 = Arduino Nano (Rev3.0)
  R1 = Resistor [tolerance=±5% resistance=220 package="0402 [SMD]"]
  R2 = Resistor [tolerance=±5% resistance=220 package="0402 [SMD]"]

nets:
  N1: Part1.S, Componente1.GND
  N2: Part1.Vin, R1.Pin_1
  N3: Part1.-, R2.Pin_1
  N4: Componente1.D10, R2.Pin_0
  N5: Componente1.D11/MOSI, R1.Pin_0

custom parts:
  KY-011 Two Color LED Module: KEYES KY-011 Two Color LED Module consist of a common cathode 3mm red/green LED.
