# Fritzing sketch KY-015 (saved by Fritzing 0.9.3b)
breadboards: 1

parts:
  Componente3 = Arduino Nano (Rev3.0)
  Part1 = KY-015 Temperature & Humidity Sensor Module [package="Breakout board"]

nets:
  N1: Componente3.GND, Part1.-
  N2: Componente3.D8, Part1.S
  5V: Componente3.5V, Part1.Vin

custom parts:
  KY-015 Temperature & Humidity Sensor Module: KY-015 temperature and humidity sensor module, provides a low-latency serial interface to measure humidity and temperature.
